# Fritzing sketch Water Level Detector (saved by Fritzing 0.8.3b)

parts:
  Q1 = NPN-Transistor [package="TO92 [THT]"]
  R1 = Resistor [tolerance=±5% resistance=220 package=THT]
  J2 = Buzzer
  VCC1 = Battery block 9V

nets:
  N1: Q1.E, VCC1.-
  N2: Q1.B, R1.Pin_0
  N3: Q1.C, J2.pin1
  N4: J2.pin2, VCC1.+

custom parts:
  Buzzer: Fixed frequency buzzer
